# Fritzing sketch arduino_button_led (saved by Fritzing 0.9.3b)
breadboards: 1

parts:
  パーツ1 = Arduino Leonardo (Rev3b)
  R1 = Resistor [tolerance=±5% resistance=10k package=THT]
  S1 = Pushbutton [package="[THT]"]
  LED1 = LED - 5mm [color="Red (633nm)" package="5 mm [THT]"]
  R2 = Resistor [tolerance=±5% resistance=330 package=THT]

nets:
  N1: パーツ1.D2/SDA, R1.Pin_1, S1.Pin_3, S1.Pin_4
  N2: パーツ1.5V, S1.Pin_1, S1.Pin_2
  N3: パーツ1.GND, R1.Pin_0, LED1.cathode
  N4: パーツ1.D13_PWM, R2.Pin_0
  N5: LED1.anode, R2.Pin_1

notes:
  330Ω
  1000Ω
