# Fritzing sketch arduino_cds (saved by Fritzing 0.9.3b)
breadboards: 1

parts:
  パーツ2 = Arduino Leonardo (Rev3b)
  R3 = Resistor [tolerance=±5% resistance=10k package=THT]
  R5 = PHOTOCELL [package=photocell-kit]

nets:
  N1: パーツ2.5V, R5.P$2
  N2: パーツ2.GND, R3.Pin_0
  N3: パーツ2.A0, R3.Pin_1, R5.P$1

notes:
  1000Ω
