# Fritzing sketch arduino_cds_led (saved by Fritzing 0.9.3b)
breadboards: 1

parts:
  パーツ2 = Arduino Leonardo (Rev3b)
  R3 = Resistor [tolerance=±5% resistance=10k package=THT]
  LED2 = LED - 5mm [color="Red (633nm)" package="5 mm [THT]"]
  R4 = Resistor [tolerance=±5% resistance=330 package=THT]
  R5 = PHOTOCELL [package=photocell-kit]

nets:
  N1: パーツ2.5V, R5.P$2
  N2: パーツ2.GND, R3.Pin_0, LED2.cathode
  N3: パーツ2.A0, R3.Pin_1, R5.P$1
  N4: パーツ2.D9_PWM/A9, R4.Pin_0
  N5: LED2.anode, R4.Pin_1

notes:
  330Ω
  1000Ω
