# Fritzing sketch arduino_dimmer (saved by Fritzing 0.9.3b)

parts:
  パーツ2 = Arduino Leonardo (Rev3b)
  RE1 = Rotary Encoder [package=THT]

nets:
  N1: パーツ2.5V, RE1.EncoderPinB
  N2: パーツ2.GND, RE1.EncoderPinA
  N3: パーツ2.A0, RE1.EncoderPinC
