# Fritzing sketch arduino_dimmer_led (saved by Fritzing 0.9.3b)
breadboards: 1

parts:
  パーツ2 = Arduino Leonardo (Rev3b)
  LED2 = LED - 5mm [color="Red (633nm)" package="5 mm [THT]"]
  R4 = Resistor [tolerance=±5% resistance=330 package=THT]
  RE1 = Rotary Encoder [package=THT]

nets:
  N1: パーツ2.5V, RE1.EncoderPinB
  N2: パーツ2.GND, LED2.cathode, RE1.EncoderPinA
  N3: パーツ2.A0, RE1.EncoderPinC
  N4: パーツ2.D9_PWM/A9, R4.Pin_0
  N5: LED2.anode, R4.Pin_1

notes:
  330Ω
